# Fritzing sketch blink-sketch (saved by Fritzing 0.9.2b)
breadboards: 1

parts:
  Часть1 = Arduino Uno (Rev3)
  R1 = Resistor [tolerance=±5% resistance=220 package=THT]
  LED2 = LED - 5mm [color="Red (633nm)" package="5 mm [THT]"]

nets:
  N1: Часть1.D13/SCK, R1.Pin_1
  N2: Часть1.GND, LED2.cathode
  N3: R1.Pin_0, LED2.anode
