# Fritzing sketch traffic-light-sketch (saved by Fritzing 0.9.2b)
breadboards: 1

parts:
  Часть1 = Arduino Uno (Rev3)
  R1 = Resistor [tolerance=±5% resistance=220 package=THT]
  LED1 = LED - 5mm [color="Red (633nm)" package="5 mm [THT]"]
  R2 = Resistor [tolerance=±5% resistance=220 package=THT]
  LED2 = LED - 5mm [color="Yellow (595nm)" package="5 mm [THT]"]
  R3 = Resistor [tolerance=±5% resistance=220 package=THT]
  LED3 = LED - 5mm [color="Green (560nm)" package="5 mm [THT]"]

nets:
  N1: Часть1.D8, R2.Pin_0
  N2: Часть1.D12/MISO, R1.Pin_0
  N3: Часть1.D2, R3.Pin_0
  N4: R1.Pin_1, LED1.anode
  GND: LED1.cathode, LED2.cathode, LED3.cathode
  N5: R2.Pin_1, LED2.anode
  N6: R3.Pin_1, LED3.anode
