# Fritzing sketch light-meter-sketch (saved by Fritzing 0.9.2b)
breadboards: 1

parts:
  Часть1 = Arduino Uno (Rev3)
  R1 = Resistor [tolerance=±5% resistance=10k package=THT]
  R2 = Photocell (LDR) [package=THT]

nets:
  N1: Часть1.A0, R1.Pin_0, R2.pin_1
  N2: Часть1.GND, R2.pin_0
  N3: Часть1.5V, R1.Pin_1
