# Fritzing sketch btn-led-switcher-sketch (saved by Fritzing 0.9.2b)
breadboards: 1

parts:
  Часть1 = Arduino Uno (Rev3)
  R1 = Resistor [tolerance=±5% resistance=220 package=THT]
  LED1 = LED - 5mm [color="Red (633nm)" package="5 mm [THT]"]
  S1 = Pushbutton [package="[THT]"]

nets:
  N1: Часть1.D12/MISO, R1.Pin_1
  N2: Часть1.GND, LED1.cathode, S1.Pin_1, S1.Pin_2
  N3: Часть1.D7, S1.Pin_3, S1.Pin_4
  N4: R1.Pin_0, LED1.anode
