# Fritzing sketch zummer-sketch (saved by Fritzing 0.9.2b)
breadboards: 1

parts:
  Часть1 = Arduino Uno (Rev3)
  J1 = Piezo Speaker
  R1 = Trimmer Potentiometer [maximum_resistance=10kΩ package=THT]

nets:
  N1: Часть1.A0, R1.wiper
  N2: Часть1.GND, J1.pin1, R1.leg2
  N3: Часть1.D7, J1.pin2
  N4: Часть1.5V, R1.leg1
